// Logisim project tennisScoreboard.circ as structural Verilog
module sevenSegment1 (
  input  Q1,
  input  Q0,
  output A,
  output B,
  output C,
  output D,
  output E,
  output F,
  output G
);

  wire and_3_out, and_4_out, not_1_out;

  not not_1 (not_1_out, Q1);
  not not_2 (D, Q0);
  and and_1 (A, Q1, D);
  or or_1 (B, Q0, Q1);
  or or_2 (C, Q0, Q1);
  and and_2 (E, not_1_out, D);
  and and_3 (and_3_out, not_1_out, D);
  and and_4 (and_4_out, Q1, Q0);
  or or_3 (F, and_3_out, and_4_out);

  assign G = Q1;
endmodule

module sevenSegment0 (
  input  Q1,
  input  Q0,
  output A,
  output B,
  output C,
  output D,
  output E,
  output F,
  output G
);

  wire not_2_out;

  not not_1 (G, Q1);
  not not_2 (not_2_out, Q0);
  or or_1 (A, Q0, Q1);
  or or_2 (E, not_2_out, Q1);
  or or_3 (F, Q0, Q1);

  assign B = Q1;
  assign C = 1'b1;
  assign D = 1'b1;
endmodule

module internalCircuit (
  input  D,
  input  reset,
  input  P,
  output Q1_out,
  output Q0_out
);

  wire and_1_out, and_2_out, not_1_out, not_2_out, or_1_out, or_2_out, Q0_qn, Q1_qn;

  not not_1 (not_1_out, D);
  not not_2 (not_2_out, not_1_out);
  and and_1 (and_1_out, Q0_out, not_1_out);
  and and_2 (and_2_out, not_2_out, Q0_qn);
  J_K_Flip_Flop Q1 (.J(and_1_out), .K(and_2_out), .clk(P), .Q(Q1_out), .Qn(Q1_qn), .reset(reset));  // open: preset
  or or_1 (or_1_out, not_1_out, Q1_out);
  J_K_Flip_Flop Q0 (.J(or_1_out), .K(or_2_out), .clk(P), .Q(Q0_out), .Qn(Q0_qn), .reset(reset));  // open: preset
  or or_2 (or_2_out, not_2_out, Q1_qn);
endmodule

module scoreboard (
  input  Player1_P,
  input  Player2_P,
  input  Delete,
  input  Reset
);

  wire internalcircuit_1_q0_out, internalcircuit_1_q1_out, internalcircuit_2_q0_out,
       internalcircuit_2_q1_out, sevensegment0_1_a, sevensegment0_1_b, sevensegment0_1_c, sevensegment0_1_d,
       sevensegment0_1_e, sevensegment0_1_f, sevensegment0_1_g, sevensegment0_2_a, sevensegment0_2_b,
       sevensegment0_2_c, sevensegment0_2_d, sevensegment0_2_e, sevensegment0_2_f, sevensegment0_2_g,
       sevensegment1_1_a, sevensegment1_1_b, sevensegment1_1_c, sevensegment1_1_d, sevensegment1_1_e,
       sevensegment1_1_f, sevensegment1_1_g, sevensegment1_2_a, sevensegment1_2_b, sevensegment1_2_c,
       sevensegment1_2_d, sevensegment1_2_e, sevensegment1_2_f, sevensegment1_2_g;

  sevenSegment1 sevensegment1_1 (
    .Q1(internalcircuit_1_q1_out), .Q0(internalcircuit_1_q0_out), .A(sevensegment1_1_a),
    .B(sevensegment1_1_b), .C(sevensegment1_1_c), .D(sevensegment1_1_d), .E(sevensegment1_1_e),
    .F(sevensegment1_1_f), .G(sevensegment1_1_g));
  sevenSegment0 sevensegment0_1 (
    .Q1(internalcircuit_1_q1_out), .Q0(internalcircuit_1_q0_out), .A(sevensegment0_1_a),
    .B(sevensegment0_1_b), .C(sevensegment0_1_c), .D(sevensegment0_1_d), .E(sevensegment0_1_e),
    .F(sevensegment0_1_f), .G(sevensegment0_1_g));
  internalCircuit internalcircuit_1 (
    .D(Delete), .reset(Reset), .P(Player1_P), .Q1_out(internalcircuit_1_q1_out),
    .Q0_out(internalcircuit_1_q0_out));
  _7_Segment_Display u_7_segment_display_1 (
    .g(sevensegment1_1_g), .f(sevensegment1_1_f), .a(sevensegment1_1_a), .b(sevensegment1_1_b),
    .e(sevensegment1_1_e), .d(sevensegment1_1_d), .c(sevensegment1_1_c));  // open: dp
  _7_Segment_Display u_7_segment_display_2 (
    .g(sevensegment0_1_g), .f(sevensegment0_1_f), .a(sevensegment0_1_a), .b(sevensegment0_1_b),
    .e(sevensegment0_1_e), .d(sevensegment0_1_d), .c(sevensegment0_1_c));  // open: dp
  sevenSegment1 sevensegment1_2 (
    .Q1(internalcircuit_2_q1_out), .Q0(internalcircuit_2_q0_out), .A(sevensegment1_2_a),
    .B(sevensegment1_2_b), .C(sevensegment1_2_c), .D(sevensegment1_2_d), .E(sevensegment1_2_e),
    .F(sevensegment1_2_f), .G(sevensegment1_2_g));
  sevenSegment0 sevensegment0_2 (
    .Q1(internalcircuit_2_q1_out), .Q0(internalcircuit_2_q0_out), .A(sevensegment0_2_a),
    .B(sevensegment0_2_b), .C(sevensegment0_2_c), .D(sevensegment0_2_d), .E(sevensegment0_2_e),
    .F(sevensegment0_2_f), .G(sevensegment0_2_g));
  internalCircuit internalcircuit_2 (
    .D(Delete), .reset(Reset), .P(Player2_P), .Q1_out(internalcircuit_2_q1_out),
    .Q0_out(internalcircuit_2_q0_out));
  _7_Segment_Display u_7_segment_display_3 (
    .g(sevensegment1_2_g), .f(sevensegment1_2_f), .a(sevensegment1_2_a), .b(sevensegment1_2_b),
    .e(sevensegment1_2_e), .d(sevensegment1_2_d), .c(sevensegment1_2_c));  // open: dp
  _7_Segment_Display u_7_segment_display_4 (
    .g(sevensegment0_2_g), .f(sevensegment0_2_f), .a(sevensegment0_2_a), .b(sevensegment0_2_b),
    .e(sevensegment0_2_e), .d(sevensegment0_2_d), .c(sevensegment0_2_c));  // open: dp
endmodule
